// Logisim project 4-bit comparator.circ as structural Verilog: 1 circuit, main circuit main
module main (
  input  in_1,
  input  in_2,
  input  in_3,
  input  in_4,
  input  in_5,
  input  in_6,
  input  in_7,
  input  in_8
);

  wire and_1_out, and_2_out, and_3_out, and_4_out, and_5_out, and_6_out, and_7_out, comparator_1_eq,
       comparator_1_gt, comparator_1_lt, comparator_2_eq, comparator_2_gt, comparator_2_lt, comparator_3_eq,
       comparator_3_gt, comparator_3_lt, comparator_4_eq, comparator_4_gt, comparator_4_lt, or_1_out,
       or_2_out;

  Comparator #(.width(1), .mode("unsigned")) comparator_1 (
    .a(in_1), .b(in_5), .gt(comparator_1_gt), .eq(comparator_1_eq), .lt(comparator_1_lt));
  Comparator #(.width(1), .mode("unsigned")) comparator_2 (
    .a(in_2), .b(in_6), .gt(comparator_2_gt), .eq(comparator_2_eq), .lt(comparator_2_lt));
  and and_1 (and_1_out, comparator_2_gt, comparator_1_eq);
  and and_2 (and_2_out, comparator_2_lt, comparator_1_eq);
  Comparator #(.width(1), .mode("unsigned")) comparator_3 (
    .a(in_3), .b(in_7), .gt(comparator_3_gt), .eq(comparator_3_eq), .lt(comparator_3_lt));
  and and_3 (and_3_out, comparator_3_gt, comparator_2_eq);
  and and_4 (and_4_out, comparator_3_lt, comparator_2_eq);
  Comparator #(.width(1), .mode("unsigned")) comparator_4 (
    .a(in_4), .b(in_8), .gt(comparator_4_gt), .eq(comparator_4_eq), .lt(comparator_4_lt));
  and and_5 (and_5_out, comparator_4_gt, comparator_3_eq);
  and and_6 (and_6_out, comparator_4_eq, comparator_3_eq, comparator_2_eq, comparator_1_eq);
  and and_7 (and_7_out, comparator_4_lt, comparator_3_eq);
  or or_1 (or_1_out, and_5_out, and_3_out, and_1_out, comparator_1_gt);
  LED led_1 (.in(or_1_out));
  LED led_2 (.in(and_6_out));
  or or_2 (or_2_out, comparator_1_lt, and_7_out, and_4_out, and_2_out);
  LED led_3 (.in(or_2_out));
endmodule
