// Logisim project 4-bit cuber.circ as structural Verilog: 1 circuit, main circuit main
module main (
  input  in_1,
  input  in_2,
  input  in_3,
  input  in_4
);

  wire and_1_out, and_2_out, and_3_out, and_4_out, and_5_out, and_6_out, and_7_out, and_8_out, and_9_out,
       and_10_out, and_11_out, and_12_out, and_13_out, and_14_out, and_15_out, and_16_out, and_17_out,
       and_18_out, and_19_out, and_20_out, and_21_out, and_22_out, not_1_out, not_2_out, not_3_out,
       not_4_out, not_5_out, or_1_out, or_2_out, or_3_out, or_4_out, or_5_out, or_6_out, or_7_out, or_8_out,
       or_9_out, xor_1_out, xor_2_out;

  not not_1 (not_1_out, in_2);
  not not_2 (not_2_out, in_1);
  not not_3 (not_3_out, in_3);
  not not_4 (not_4_out, in_4);
  or or_1 (or_1_out, in_4, in_3);
  LED led_1 (.in(or_2_out));
  LED led_2 (.in(and_1_out));
  and and_1 (and_1_out, or_1_out, in_2, in_1);
  or or_2 (or_2_out, and_2_out, and_3_out);
  and and_2 (and_2_out, in_1, in_3, in_4);
  and and_3 (and_3_out, in_1, in_2, not_3_out, not_4_out);
  and and_4 (and_4_out, in_4, not_3_out, in_2, not_2_out);
  and and_5 (and_5_out, in_3, in_1);
  xor xor_1 (xor_1_out, in_3, in_4);
  and and_6 (and_6_out, not_4_out, in_2, in_3);
  and and_7 (and_7_out, not_3_out, in_1, in_2);
  and and_8 (and_8_out, in_2, in_3, in_4);
  and and_9 (and_9_out, in_3, in_1, not_1_out);
  LED led_3 (.in(or_3_out));
  or or_3 (or_3_out, and_11_out, and_10_out);
  and and_10 (and_10_out, in_1, not_4_out);
  and and_11 (and_11_out, in_1, not_1_out, not_3_out);
  and and_12 (and_12_out, not_2_out, in_2);
  and and_13 (and_13_out, in_2, not_3_out, not_4_out);
  and and_14 (and_14_out, in_1, not_1_out, xor_1_out);
  or or_4 (or_4_out, and_9_out, and_8_out);
  or or_5 (or_5_out, and_7_out, and_6_out, and_14_out);
  LED led_4 (.in(or_4_out));
  or or_6 (or_6_out, and_14_out, and_13_out, and_12_out);
  LED led_5 (.in(or_6_out));
  LED led_6 (.in(or_5_out));
  LED led_7 (.in(or_7_out));
  or or_7 (or_7_out, and_4_out, and_5_out);
  and and_15 (and_15_out, in_4, not_1_out, in_1);
  and and_16 (and_16_out, not_2_out, in_4, in_3);
  and and_17 (and_17_out, xor_1_out, in_2);
  or or_8 (or_8_out, and_17_out, and_16_out, and_15_out);
  LED led_8 (.in(or_8_out));
  and and_18 (and_18_out, in_3, not_4_out);
  LED led_9 (.in(or_9_out));
  and and_19 (and_19_out, in_4, not_3_out, xor_2_out);
  and and_20 (and_20_out, in_3, not_5_out);
  not not_5 (not_5_out, xor_2_out);
  xor xor_2 (xor_2_out, in_2, in_1);
  LED led_10 (.in(and_21_out));
  and and_21 (and_21_out, in_4, in_2);
  or or_9 (or_9_out, and_19_out, and_18_out, and_20_out);
  LED led_11 (.in(in_4));
  LED led_12 (.in(and_22_out));
  and and_22 (and_22_out, in_4, in_3);
endmodule
