// Logisim project 4-bit squarer.circ as structural Verilog: 1 circuit, main circuit main
module main (
  input  A,
  input  B,
  input  C,
  input  D
);

  wire and_1_out, and_2_out, and_3_out, and_4_out, and_5_out, and_6_out, and_7_out, and_8_out, not_1_out,
       not_2_out, not_3_out, or_1_out, or_2_out, or_3_out, xor_1_out, xor_2_out;

  not not_1 (not_1_out, B);
  not not_2 (not_2_out, D);
  not not_3 (not_3_out, C);
  or or_1 (or_1_out, not_1_out, C);
  and and_1 (and_1_out, C, not_2_out);
  and and_2 (and_2_out, B, A);
  LED led_1 (.in(and_2_out));
  and and_3 (and_3_out, A, or_1_out);
  and and_4 (and_4_out, A, D, B);
  xor xor_1 (xor_1_out, B, A);
  and and_5 (and_5_out, B, not_3_out, not_2_out);
  xor xor_2 (xor_2_out, C, B);
  LED led_2 (.in(and_3_out));
  or or_2 (or_2_out, and_4_out, and_6_out);
  and and_6 (and_6_out, C, xor_1_out);
  and and_7 (and_7_out, xor_1_out, D);
  and and_8 (and_8_out, xor_2_out, D);
  LED led_3 (.in(or_2_out));
  LED led_4 (.in(or_3_out));
  or or_3 (or_3_out, and_5_out, and_7_out);
  LED led_5 (.in(and_8_out));
  LED led_6 (.in(and_1_out));
  LED led_7 ();  // open: in
  LED led_8 (.in(D));
endmodule
