// Logisim project [D] 0-15-0 counter.circ as structural Verilog: 1 circuit, main circuit main
module main (
  input  Mode
);

  wire A_q, A_qn, and_1_out, and_2_out, and_3_out, and_4_out, and_5_out, and_6_out, and_7_out, and_8_out,
       and_9_out, and_10_out, and_11_out, B_q, B_qn, C_q, C_qn, clock_1_out, D_q, D_qn, not_1_out, not_2_out,
       or_1_out, or_2_out, or_3_out, or_4_out, or_5_out, or_6_out, xnor_1_out, xnor_2_out, xor_1_out,
       xor_2_out, xor_3_out;

  not not_1 (not_1_out, Mode);
  Clock clock_1 (.out(clock_1_out));
  D_Flip_Flop A (.clk(clock_1_out), .D(or_5_out), .Q(A_q), .Qn(A_qn));  // open: preset, en, reset
  LED led_1 (.in(A_q));
  D_Flip_Flop B (.clk(clock_1_out), .D(or_6_out), .Q(B_q), .Qn(B_qn));  // open: preset, en, reset
  LED led_2 (.in(B_q));
  or or_1 (or_1_out, and_1_out, and_2_out);
  and and_1 (and_1_out, not_1_out, xor_1_out);
  xor xor_1 (xor_1_out, D_q, C_q);
  D_Flip_Flop C (.clk(clock_1_out), .D(or_1_out), .Q(C_q), .Qn(C_qn));  // open: preset, en, reset
  and and_2 (and_2_out, not_2_out, Mode);
  not not_2 (not_2_out, xor_1_out);
  LED led_3 (.in(C_q));
  D_Flip_Flop D (.clk(clock_1_out), .D(D_qn), .Q(D_q), .Qn(D_qn));  // open: preset, en, reset
  xor xor_2 (xor_2_out, D_q, C_q);
  LED led_4 (.in(D_q));
  xor xor_3 (xor_3_out, C_q, D_q);
  xnor xnor_1 (xnor_1_out, Mode, D_q);
  or or_2 (or_2_out, xnor_1_out, xor_2_out);
  and and_3 (and_3_out, D_q, C_q, B_qn, A_q);
  and and_4 (and_4_out, C_qn, B_q, A_q);
  and and_5 (and_5_out, not_1_out, D_q, C_q, B_q, A_qn);
  and and_6 (and_6_out, A_qn, B_qn, C_qn, D_qn, Mode);
  or or_3 (or_3_out, xor_3_out, xnor_2_out);
  xnor xnor_2 (xnor_2_out, D_q, Mode);
  and and_7 (and_7_out, C_q, D_q, not_1_out);
  and and_8 (and_8_out, Mode, C_qn, D_qn);
  and and_9 (and_9_out, or_3_out, A_q);
  or or_4 (or_4_out, and_7_out, and_8_out);
  and and_10 (and_10_out, B_q, or_2_out);
  and and_11 (and_11_out, or_4_out, B_qn);
  or or_5 (or_5_out, and_3_out, and_4_out, and_5_out, and_6_out, and_9_out);
  or or_6 (or_6_out, and_10_out, and_11_out);
endmodule
